// Logisim project C-ALU.circ as structural Verilog: 1 circuit, main circuit ALU
module ALU (
  input  [31:0] in_1,
  input  [31:0] in_2,
  input  [3:0] in_3,
  output [31:0] out_4,
  output [31:0] out_5,
  output [31:0] out_6,
  output ZeroFlag,
  output NegativeFlag
);

  wire comparator_2_lt, comparator_3_lt, enable;
  wire [31:0] add, \and , div, multHi, multLo, \nor , \or , rem, slt, sltu, sub, \xor ;

  Adder #(.width(32)) adder_1 (.a(in_1), .b(in_2), .out(add));  // open: cin, cout
  Subtractor #(.width(32)) subtractor_1 (.a(in_1), .b(in_2), .out(sub));  // open: bin, bout
  Multiplier #(.width(32)) multiplier_1 (.a(in_1), .b(in_2), .out(multLo), .cout(multHi));  // open: cin
  Divider #(.width(32)) divider_1 (.a(in_1), .b(in_2), .out(div), .rem(rem));  // open: upper
  Multiplexer #(.select(4), .width(32), .enable("false")) multiplexer_1 (
    .in0(add), .in1(sub), .in2(slt), .in3(sltu), .in4({32{1'b0}}), .in5({32{1'b0}}), .in6({32{1'b0}}),
    .in7({32{1'b0}}), .in8(\and ), .in9(\or ), .in10(\nor ), .in11(\xor ), .out(out_4), .sel(in_3));  // open: in12, in13, in14, in15
  assign \and  = in_1 & in_2;  // AND_Gate and_1, 32 bits wide
  assign \or  = in_1 | in_2;  // OR_Gate or_1, 32 bits wide
  assign \nor  = ~(in_1 | in_2);  // NOR_Gate nor_1, 32 bits wide
  assign \xor  = in_1 ^ in_2;  // XOR_Gate xor_1, 32 bits wide
  Comparator #(.width(2)) comparator_1 (.a(in_3[3:2]), .b(2'b01), .eq(enable));  // open: gt, lt
  Comparator #(.width(32)) comparator_2 (.a(in_1), .b(in_2), .lt(comparator_2_lt));  // open: gt, eq
  Comparator #(.width(32), .mode("unsigned")) comparator_3 (.a(in_1), .b(in_2), .lt(comparator_3_lt));  // open: gt, eq
  Multiplexer #(.width(32), .enable("false")) multiplexer_2 (
    .in0({32{1'b0}}), .in1(32'h1), .out(slt), .sel(comparator_2_lt));
  Multiplexer #(.width(32), .enable("false")) multiplexer_3 (
    .in0({32{1'b0}}), .in1(32'h1), .out(sltu), .sel(comparator_3_lt));
  Multiplexer #(.select(2), .width(32)) multiplexer_4 (
    .in0(multLo), .in2(div), .out(out_5), .sel(in_3[1:0]), .en(enable));  // open: in1, in3
  Comparator #(.width(32)) comparator_4 (.a(out_4), .b({32{1'b0}}), .eq(ZeroFlag), .lt(NegativeFlag));  // open: gt
  Multiplexer #(.select(2), .width(32)) multiplexer_5 (
    .in0(multHi), .in2(rem), .out(out_6), .sel(in_3[1:0]), .en(enable));  // open: in1, in3

  // Other names for the same wires on the sheet: A[31:0] = in_1; B[31:0] = in_2; High[31:0] = out_6;
  //   Low[31:0] = out_5; opcode[3:0] = in_3; oplo[1:0] = in_3[1:0]; ophi[1:0] = in_3[3:2]; result[31:0] = out_4

  // Notes on the sheet:
  //   Operaciones
  //   Add    0
  //   Sub    1
  //   Slt    2
  //   Sltu    3
  //   Mult    4  0100
  //   Multu    5 0101
  //   Div    6 0110
  //   Divu    7 0111
  //   Determinar si se efectua una operacion que modifica el low o el high (01 high order bits)
  //   Opcodes
  //   And    8
  //   Or    9
  //   Nor   10
  //   Xor   11
  //   Flags
endmodule
