// Logisim project C-ControlUnit.circ as structural Verilog
module ControlUnit (
  input  CLK,
  input  RST,
  input  ZERO_FLAG,
  input  [5:0] CODE,
  input  NEGATIVE_FLAG,
  input  End_Fectch_Instruction,
  input  Instruction_Avaiable,
  output Start_Fectch_Instruction,
  output STOP,
  output LoadInstructionRegister,
  output Load_PC,
  output TTY_ENABLE,
  output [1:0] BRANCH_SELECTOR,
  output WRITE_RF,
  output [1:0] ADDRESS_SELECTOR,
  output [1:0] DATA_SELECTOR,
  output LOAD_LO,
  output LOAD_HI,
  output [3:0] ALU_OP_SELECTOR,
  output [1:0] ALU_SELECTOR_A,
  output [2:0] ALU_SELECTOR_B
);

  wire ADD, ADDI, ADDI_END, ADDI_SELECTOR_ADDRESS0, ALU_ADD_SELECTOR_A0, ALU_ADD_SELECTOR_B0,
       ALU_ADDI_SELECTOR_A0, ALU_ADDI_SELECTOR_B0, ALU_ADDI_SELECTOR_B1, ALU_AND_SELECTOR_A0,
       ALU_AND_SELECTOR_B0, ALU_AND_SELECTOR_OP3, ALU_ANDI_SELECTOR_A0, ALU_ANDI_SELECTOR_B0,
       ALU_ANDI_SELECTOR_B1, ALU_ANDI_SELECTOR_OP3, ALU_BEQ_SELECTOR_A0, ALU_BEQ_SELECTOR_B0,
       ALU_BEQ_SELECTOR_B2, ALU_BEQ_SELECTOR_OP0, ALU_BGTZ_SELECTOR_A0, ALU_BGTZ_SELECTOR_B0,
       ALU_BGTZ_SELECTOR_B1, ALU_BGTZ_SELECTOR_B2, ALU_BGTZ_SELECTOR_OP0, ALU_BLEZ_SELECTOR_A0,
       ALU_BLEZ_SELECTOR_B0, ALU_BLEZ_SELECTOR_B1, ALU_BLEZ_SELECTOR_B2, ALU_BLEZ_SELECTOR_OP0,
       ALU_BLTZ_SELECTOR_A0, ALU_BLTZ_SELECTOR_B0, ALU_BLTZ_SELECTOR_B1, ALU_BLTZ_SELECTOR_B2,
       ALU_BLTZ_SELECTOR_OP0, ALU_BNE_SELECTOR_A0, ALU_BNE_SELECTOR_B0, ALU_BNE_SELECTOR_B2,
       ALU_BNE_SELECTOR_OP0, ALU_DIV_SELECTOR_A0, ALU_DIV_SELECTOR_B0, ALU_DIV_SELECTOR_OP1,
       ALU_DIV_SELECTOR_OP2, ALU_DIVU_SELECTOR_A0, ALU_DIVU_SELECTOR_B0, ALU_DIVU_SELECTOR_OP0,
       ALU_DIVU_SELECTOR_OP1, ALU_DIVU_SELECTOR_OP2, ALU_MULT_SELECTOR_A0, ALU_MULT_SELECTOR_B0,
       ALU_MULT_SELECTOR_OP2, ALU_MULTU_SELECTOR_A0, ALU_MULTU_SELECTOR_B0, ALU_MULTU_SELECTOR_OP0,
       ALU_MULTU_SELECTOR_OP2, ALU_NOR_SELECTOR_A0, ALU_NOR_SELECTOR_B0, ALU_NOR_SELECTOR_OP1,
       ALU_NOR_SELECTOR_OP3, ALU_OR_SELECTOR_A0, ALU_OR_SELECTOR_B0, ALU_OR_SELECTOR_OP0,
       ALU_OR_SELECTOR_OP3, ALU_ORI_SELECTOR_A0, ALU_ORI_SELECTOR_B0, ALU_ORI_SELECTOR_B1,
       ALU_ORI_SELECTOR_OP0, ALU_ORI_SELECTOR_OP3, ALU_SLT_SELECTOR_A0, ALU_SLT_SELECTOR_B0,
       ALU_SLT_SELECTOR_OP1, ALU_SLTI_SELECTOR_A0, ALU_SLTI_SELECTOR_B0, ALU_SLTI_SELECTOR_B1,
       ALU_SLTI_SELECTOR_OP1, ALU_SLTIU_SELECTOR_A0, ALU_SLTIU_SELECTOR_B0, ALU_SLTIU_SELECTOR_B1,
       ALU_SLTIU_SELECTOR_OP0, ALU_SLTIU_SELECTOR_OP1, ALU_SLTU_SELECTOR_A0, ALU_SLTU_SELECTOR_B0,
       ALU_SLTU_SELECTOR_OP0, ALU_SLTU_SELECTOR_OP1, ALU_SUB_SELECTOR_A0, ALU_SUB_SELECTOR_B0,
       ALU_SUB_SELECTOR_OP0, ALU_XOR_SELECTOR_A0, ALU_XOR_SELECTOR_B0, ALU_XOR_SELECTOR_OP0,
       ALU_XOR_SELECTOR_OP1, ALU_XOR_SELECTOR_OP3, ALU_XORI_SELECTOR_A0, ALU_XORI_SELECTOR_B0,
       ALU_XORI_SELECTOR_B1, ALU_XORI_SELECTOR_OP0, ALU_XORI_SELECTOR_OP1, ALU_XORI_SELECTOR_OP3, AND, ANDI,
       ANDI_END, ANDI_SELECTOR_ADDRESS0, BEQ, BEQ_END, BGTZ, BGTZ_END, BLEZ, BLEZ_END, BLTZ, BLTZ_END, BNE,
       BNE_END, d_ff_1_q, demultiplexer_1_out0, demultiplexer_1_out1, demultiplexer_2_out0,
       demultiplexer_2_out1, DIV, DIVU, END_ADD, END_AND, END_DIV, END_DIVU, END_HALT, END_MULT, END_MULTU,
       END_NOP, END_NOR, END_OR, END_SUB, END_TTY, END_XOR, Forward_PC, HALT, INVALID, J, J_END, JR, JR_END,
       KBD, LOAD_HI_DIV, LOAD_HI_DIVU, LOAD_HI_MULT, LOAD_HI_MULTU, LOAD_LO_DIV, LOAD_LO_DIVU, LOAD_LO_MULT,
       LOAD_LO_MULTU, LOAD_PC_0, LOAD_PC_BEQ, LOAD_PC_BGTZ, LOAD_PC_BLEZ, LOAD_PC_BLTZ, LOAD_PC_BNE, LW,
       MFHI, MFHI_END, MFHI_SELECTOR_DATA0, MFLO, MFLO_END, MFLO_SELECTOR_DATA0, MULT, Multi_Cycle, MULTU,
       NOP, NOR, OR, or_1_out, or_5_out, or_8_out, or_10_out, or_12_out, or_13_out, or_14_out, or_15_out,
       or_18_out, or_19_out, or_20_out, or_21_out, or_22_out, or_23_out, or_24_out, or_25_out, or_32_out,
       or_35_out, ORI, ORI_END, ORI_SELECTOR_ADDRESS0, POP, PUSH, RND, Salto, Single_Cycle, SLT,
       SLTI_SELECTOR_ADDRESS0, SLTIU_SELECTOR_ADDRESS0, SLTU, SLTU_END, STL_END, STLI, STLI_END, STLIU,
       STLIU_END, SUB, SW, TTY, Wait_for_instruction_fetch_q, WRITE_RF_ADD, WRITE_RF_ADDI, WRITE_RF_AND,
       WRITE_RF_ANDI, WRITE_RF_MFHI, WRITE_RF_MFLO, WRITE_RF_NOR, WRITE_RF_OR, WRITE_RF_ORI, WRITE_RF_SLT,
       WRITE_RF_SLTI, WRITE_RF_SLTIU, WRITE_RF_SLTU, WRITE_RF_SUB, WRITE_RF_XOR, WRITE_RF_XORI, XOR, XORI,
       XORI_END, XORI_SELECTOR_ADDRESS0;

  or or_1 (or_1_out, 1'b0, demultiplexer_1_out1);
  Demultiplexer #(.enable("false")) demultiplexer_1 (
    .out0(demultiplexer_1_out0), .out1(demultiplexer_1_out1), .in(d_ff_1_q), .sel(RST));
  D_Flip_Flop d_ff_1 (.clk(CLK), .D(or_1_out), .Q(d_ff_1_q), .preset(RST));  // open: Qn, en, reset
  or or_2 (Start_Fectch_Instruction, Salto, Multi_Cycle, Single_Cycle, demultiplexer_1_out0);
  or or_3 (LOAD_LO, LOAD_LO_MULT, LOAD_LO_MULTU, LOAD_LO_DIV, LOAD_LO_DIVU);
  or or_4 (LOAD_HI, LOAD_HI_MULT, LOAD_HI_MULTU, LOAD_HI_DIV, LOAD_HI_DIVU);
  or or_5 (or_5_out, demultiplexer_2_out0, Start_Fectch_Instruction);
  or or_6 (DATA_SELECTOR[0], MFHI_SELECTOR_DATA0, MFLO_SELECTOR_DATA0);
  D_Flip_Flop Wait_for_instruction_fetch (
    .clk(CLK), .D(or_5_out), .Q(Wait_for_instruction_fetch_q), .reset(RST));  // open: Qn, preset, en
  Demultiplexer #(.enable("false")) demultiplexer_2 (
    .out0(demultiplexer_2_out0), .out1(demultiplexer_2_out1), .in(Wait_for_instruction_fetch_q),
    .sel(End_Fectch_Instruction));
  or or_7 (Load_PC, LOAD_PC_0, LOAD_PC_BNE, LOAD_PC_BEQ, LOAD_PC_BGTZ, LOAD_PC_BLEZ, LOAD_PC_BLTZ);
  or or_8 (or_8_out, WRITE_RF_ADD, WRITE_RF_SUB, WRITE_RF_AND, WRITE_RF_ORI, WRITE_RF_OR, WRITE_RF_NOR, WRITE_RF_XOR, WRITE_RF_ADDI);
  or or_9 (WRITE_RF, or_8_out, or_10_out);
  or or_10 (or_10_out, WRITE_RF_MFHI, WRITE_RF_MFLO, WRITE_RF_ANDI, WRITE_RF_XORI, WRITE_RF_SLT, WRITE_RF_SLTU, WRITE_RF_SLTI, WRITE_RF_SLTIU);
  or or_11 (ADDRESS_SELECTOR[0], SLTIU_SELECTOR_ADDRESS0, ADDI_SELECTOR_ADDRESS0, ANDI_SELECTOR_ADDRESS0, ORI_SELECTOR_ADDRESS0, XORI_SELECTOR_ADDRESS0, SLTI_SELECTOR_ADDRESS0);
  or or_12 (or_12_out, ALU_BLTZ_SELECTOR_OP0, ALU_BGTZ_SELECTOR_OP0, ALU_BLEZ_SELECTOR_OP0, ALU_BNE_SELECTOR_OP0, ALU_BEQ_SELECTOR_OP0, ALU_SUB_SELECTOR_OP0, ALU_DIVU_SELECTOR_OP0, ALU_OR_SELECTOR_OP0);
  or or_13 (or_13_out, ALU_XORI_SELECTOR_OP0, ALU_XOR_SELECTOR_OP0, ALU_MULTU_SELECTOR_OP0, ALU_ORI_SELECTOR_OP0, ALU_SLTIU_SELECTOR_OP0, ALU_SLTU_SELECTOR_OP0);
  or or_14 (or_14_out, ALU_SLTI_SELECTOR_OP1, ALU_NOR_SELECTOR_OP1, ALU_SLTU_SELECTOR_OP1, ALU_SLTIU_SELECTOR_OP1, ALU_SLT_SELECTOR_OP1);
  or or_15 (or_15_out, ALU_DIV_SELECTOR_OP1, ALU_DIVU_SELECTOR_OP1, ALU_XORI_SELECTOR_OP1, ALU_XOR_SELECTOR_OP1);
  or or_16 (ALU_OP_SELECTOR[2], ALU_MULT_SELECTOR_OP2, ALU_MULTU_SELECTOR_OP2, ALU_DIV_SELECTOR_OP2, ALU_DIVU_SELECTOR_OP2);
  or or_17 (ALU_OP_SELECTOR[3], ALU_XORI_SELECTOR_OP3, ALU_ORI_SELECTOR_OP3, ALU_OR_SELECTOR_OP3, ALU_NOR_SELECTOR_OP3, ALU_XOR_SELECTOR_OP3, ALU_ANDI_SELECTOR_OP3, ALU_AND_SELECTOR_OP3);
  or or_18 (or_18_out, ALU_ADD_SELECTOR_A0, ALU_SUB_SELECTOR_A0, ALU_MULT_SELECTOR_A0, ALU_MULTU_SELECTOR_A0, ALU_DIV_SELECTOR_A0, ALU_DIVU_SELECTOR_A0, ALU_AND_SELECTOR_A0, ALU_OR_SELECTOR_A0);
  or or_19 (or_19_out, ALU_NOR_SELECTOR_A0, ALU_XOR_SELECTOR_A0, ALU_ADDI_SELECTOR_A0, ALU_ANDI_SELECTOR_A0, ALU_ORI_SELECTOR_A0, ALU_XORI_SELECTOR_A0, ALU_SLT_SELECTOR_A0, ALU_SLTU_SELECTOR_A0);
  or or_20 (or_20_out, ALU_SLTI_SELECTOR_A0, ALU_SLTIU_SELECTOR_A0, ALU_BEQ_SELECTOR_A0, ALU_BNE_SELECTOR_A0, ALU_BLEZ_SELECTOR_A0, ALU_BGTZ_SELECTOR_A0, ALU_BLTZ_SELECTOR_A0);
  or or_21 (or_21_out, ALU_ADD_SELECTOR_B0, ALU_SUB_SELECTOR_B0, ALU_MULT_SELECTOR_B0, ALU_MULTU_SELECTOR_B0, ALU_DIV_SELECTOR_B0, ALU_DIVU_SELECTOR_B0, ALU_AND_SELECTOR_B0, ALU_OR_SELECTOR_B0);
  or or_22 (or_22_out, ALU_NOR_SELECTOR_B0, ALU_XOR_SELECTOR_B0, ALU_ADDI_SELECTOR_B0, ALU_ANDI_SELECTOR_B0, ALU_ORI_SELECTOR_B0, ALU_XORI_SELECTOR_B0, ALU_SLT_SELECTOR_B0, ALU_SLTU_SELECTOR_B0);
  or or_23 (or_23_out, ALU_SLTI_SELECTOR_B0, ALU_SLTIU_SELECTOR_B0, ALU_BEQ_SELECTOR_B0, ALU_BNE_SELECTOR_B0, ALU_BLEZ_SELECTOR_B0, ALU_BGTZ_SELECTOR_B0, ALU_BLTZ_SELECTOR_B0);
  or or_24 (or_24_out, ALU_ADDI_SELECTOR_B1, ALU_ANDI_SELECTOR_B1, ALU_ORI_SELECTOR_B1, ALU_XORI_SELECTOR_B1, ALU_SLTI_SELECTOR_B1);
  or or_25 (or_25_out, ALU_SLTIU_SELECTOR_B1, ALU_BLEZ_SELECTOR_B1, ALU_BGTZ_SELECTOR_B1, ALU_BLTZ_SELECTOR_B1);
  or or_26 (ALU_SELECTOR_B[2], ALU_BEQ_SELECTOR_B2, ALU_BNE_SELECTOR_B2, ALU_BLEZ_SELECTOR_B2, ALU_BGTZ_SELECTOR_B2, ALU_BLTZ_SELECTOR_B2);
  or or_27 (ALU_OP_SELECTOR[0], or_12_out, or_13_out);
  or or_28 (ALU_OP_SELECTOR[1], or_14_out, or_15_out);
  or or_29 (ALU_SELECTOR_A[0], or_18_out, or_19_out, or_20_out);
  or or_30 (ALU_SELECTOR_B[0], or_21_out, or_22_out, or_23_out);
  or or_31 (ALU_SELECTOR_B[1], or_24_out, or_25_out);
  _6bitDemultiplexer u_6bitdemultiplexer_1 (
    .Power(demultiplexer_2_out1), ._6bit_Selector(CODE), .Output_0(NOP), .Output_1(BLTZ), .Output_2(J),
    .Output_3(JR), .Output_4(BEQ), .Output_5(BNE), .Output_6(BLEZ), .Output_7(BGTZ), .Output_8(ADDI),
    .Output_10(STLI), .Output_11(STLIU), .Output_12(ANDI), .Output_13(ORI), .Output_14(XORI),
    .Output_16(MFHI), .Output_18(MFLO), .Output_24(MULT), .Output_25(MULTU), .Output_26(DIV),
    .Output_27(DIVU), .Output_31(INVALID), .Output_32(ADD), .Output_34(SUB), .Output_35(LW), .Output_36(AND),
    .Output_37(OR), .Output_39(NOR), .Output_40(XOR), .Output_41(SLTU), .Output_42(SLT), .Output_43(SW),
    .Output_48(POP), .Output_49(PUSH), .Output_57(TTY), .Output_58(RND), .Output_60(KBD), .Output_63(HALT));  // open: Output_9, Output_15, Output_17, Output_19, Output_20, Output_21, Output_22, Output_23, Output_28, Output_29, Output_30, Output_33, Output_38, Output_44, Output_45, Output_46, Output_47, Output_50, Output_51, Output_52, Output_53, Output_54, Output_55, Output_56, Output_59, Output_61, Output_62
  J j_1 (.POWER_IN(J), .POWER_OUT(J_END), .SELECTOR_BRANCH0(BRANCH_SELECTOR[0]));
  JR jr_1 (.POWER_IN(JR), .POWER_OUT(JR_END), .SELECTOR_BRANCH1(BRANCH_SELECTOR[1]));
  or or_32 (or_32_out, STOP, END_HALT);
  D_Flip_Flop Wait_a_cycle (.clk(CLK), .D(or_32_out), .Q(STOP), .reset(RST));  // open: Qn, preset, en
  or or_33 (Forward_PC, END_NOP, END_ADD, END_SUB, END_TTY, END_MULT, END_MULTU, END_DIV, END_DIVU, END_AND, END_OR, END_NOR, END_XOR, ADDI_END, ANDI_END, ORI_END, XORI_END, STL_END, SLTU_END, STLI_END, STLIU_END, MFHI_END, MFLO_END);
  BEQ beq_1 (
    .CLK(CLK), .ZERO_FLAG(ZERO_FLAG), .SELECTOR_A0(ALU_BEQ_SELECTOR_A0), .SELECTOR_B0(ALU_BEQ_SELECTOR_B0),
    .Load_PC(LOAD_PC_BEQ), .RST(RST), .SELECTOR_OP0(ALU_BEQ_SELECTOR_OP0), .SELECTOR_B2(ALU_BEQ_SELECTOR_B2),
    .power_in(BEQ), .power_out(BEQ_END));
  BNE bne_1 (
    .CLK(CLK), .ZERO_FLAG(ZERO_FLAG), .SELECTOR_A0(ALU_BNE_SELECTOR_A0), .SELECTOR_B0(ALU_BNE_SELECTOR_B0),
    .Load_PC(LOAD_PC_BNE), .RST(RST), .SELECTOR_OP0(ALU_BNE_SELECTOR_OP0), .SELECTOR_B2(ALU_BNE_SELECTOR_B2),
    .power_in(BNE), .power_out(BNE_END));
  BLEZ blez_1 (
    .CLK(CLK), .ZERO_FLAG(ZERO_FLAG), .SELECTOR_A0(ALU_BLEZ_SELECTOR_A0), .SELECTOR_B0(ALU_BLEZ_SELECTOR_B0),
    .Load_PC(LOAD_PC_BLEZ), .RST(RST), .NEGATIVE_FLAG(NEGATIVE_FLAG), .SELECTOR_OP0(ALU_BLEZ_SELECTOR_OP0),
    .SELECTOR_B1(ALU_BLEZ_SELECTOR_B1), .power_in(BLEZ), .power_out(BLEZ_END),
    .SELECTOR_B2(ALU_BLEZ_SELECTOR_B2));
  BGTZ bgtz_1 (
    .CLK(CLK), .ZERO_FLAG(ZERO_FLAG), .SELECTOR_A0(ALU_BGTZ_SELECTOR_A0), .SELECTOR_B0(ALU_BGTZ_SELECTOR_B0),
    .Load_PC(LOAD_PC_BGTZ), .RST(RST), .NEGATIVE_FLAG(NEGATIVE_FLAG), .SELECTOR_OP0(ALU_BGTZ_SELECTOR_OP0),
    .SELECTOR_B1(ALU_BGTZ_SELECTOR_B1), .SELECTOR_B2(ALU_BGTZ_SELECTOR_B2), .power_out(BGTZ_END),
    .power_in(BGTZ));
  BLTZ bltz_1 (
    .CLK(CLK), .SELECTOR_A0(ALU_BLTZ_SELECTOR_A0), .SELECTOR_B0(ALU_BLTZ_SELECTOR_B0),
    .Load_PC(LOAD_PC_BLTZ), .RST(RST), .NEGATIVE_FLAG(NEGATIVE_FLAG), .SELECTOR_OP0(ALU_BLTZ_SELECTOR_OP0),
    .SELECTOR_B1(ALU_BLTZ_SELECTOR_B1), .SELECTOR_B2(ALU_BLTZ_SELECTOR_B2), .power_in(BLTZ),
    .power_out(BLTZ_END));
  or or_34 (Multi_Cycle, BEQ_END, BNE_END, BLEZ_END, BGTZ_END, BLTZ_END);
  or or_35 (or_35_out, J_END, JR_END);
  D_Flip_Flop d_ff_2 (.clk(CLK), .D(or_35_out), .Q(Salto), .reset(RST));  // open: Qn, preset, en
  MFHI mfhi_1 (
    .CLK(CLK), .RST(RST), .POWER_IN(MFHI), .POWER_OUT(MFHI_END), .WRITE_RF(WRITE_RF_MFHI),
    .SELECTOR_DATA0(MFHI_SELECTOR_DATA0));
  MFLO mflo_1 (
    .CLK(CLK), .RST(RST), .POWER_IN(MFLO), .POWER_OUT(MFLO_END), .WRITE_RF(WRITE_RF_MFLO),
    .SELECTOR_DATA1(MFLO_SELECTOR_DATA0));
  ANDI andi_1 (
    .CLK(CLK), .RST(RST), .POWER_IN(ANDI), .POWER_OUT(ANDI_END), .ALU_SELECTOR_A0(ALU_ANDI_SELECTOR_A0),
    .ALU_SELECTOR_B0(ALU_ANDI_SELECTOR_B0), .ALU_SELECTOR_B1(ALU_ANDI_SELECTOR_B1),
    .ALU_SELECTOR_OP3(ALU_ANDI_SELECTOR_OP3), .WRITE_RF(WRITE_RF_ANDI),
    .SELECTOR_ADDRESS0(ANDI_SELECTOR_ADDRESS0));
  ADDI addi_1 (
    .CLK(CLK), .RST(RST), .POWER_IN(ADDI), .POWER_OUT(ADDI_END), .ALU_SELECTOR_A0(ALU_ADDI_SELECTOR_A0),
    .ALU_SELECTOR_B0(ALU_ADDI_SELECTOR_B0), .ALU_SELECTOR_B1(ALU_ADDI_SELECTOR_B1), .WRITE_RF(WRITE_RF_ADDI),
    .SELECTOR_ADDRESS0(ADDI_SELECTOR_ADDRESS0));
  ORI ori_1 (
    .CLK(CLK), .RST(RST), .POWER_IN(ORI), .POWER_OUT(ORI_END), .ALU_SELECTOR_A0(ALU_ORI_SELECTOR_A0),
    .ALU_SELECTOR_B0(ALU_ORI_SELECTOR_B0), .ALU_SELECTOR_B1(ALU_ORI_SELECTOR_B1),
    .ALU_SELECTOR_OP0(ALU_ORI_SELECTOR_OP0), .ALU_SELECTOR_OP3(ALU_ORI_SELECTOR_OP3),
    .WRITE_RF(WRITE_RF_ORI), .SELECTOR_ADDRESS0(ORI_SELECTOR_ADDRESS0));
  XORI xori_1 (
    .CLK(CLK), .RST(RST), .POWER_IN(XORI), .POWER_OUT(XORI_END), .ALU_SELECTOR_A0(ALU_XORI_SELECTOR_A0),
    .ALU_SELECTOR_B0(ALU_XORI_SELECTOR_B0), .ALU_SELECTOR_B1(ALU_XORI_SELECTOR_B1),
    .ALU_SELECTOR_OP0(ALU_XORI_SELECTOR_OP0), .ALU_SELECTOR_OP1(ALU_XORI_SELECTOR_OP1),
    .ALU_SELECTOR_OP3(ALU_XORI_SELECTOR_OP3), .WRITE_RF(WRITE_RF_XORI),
    .SELECTOR_ADDRESS0(XORI_SELECTOR_ADDRESS0));
  STLI stli_1 (
    .CLK(CLK), .RST(RST), .POWER_IN(STLI), .POWER_OUT(STLI_END), .ALU_SELECTOR_A0(ALU_SLTI_SELECTOR_A0),
    .ALU_SELECTOR_B0(ALU_SLTI_SELECTOR_B0), .ALU_SELECTOR_B1(ALU_SLTI_SELECTOR_B1),
    .ALU_SELECTOR_OP1(ALU_SLTI_SELECTOR_OP1), .WRITE_RF(WRITE_RF_SLTI),
    .SELECTOR_ADDRESS0(SLTI_SELECTOR_ADDRESS0));
  SLTIU sltiu_1 (
    .CLK(CLK), .RST(RST), .POWER_IN(STLIU), .POWER_OUT(STLIU_END), .ALU_SELECTOR_A0(ALU_SLTIU_SELECTOR_A0),
    .ALU_SELECTOR_B0(ALU_SLTIU_SELECTOR_B0), .ALU_SELECTOR_B1(ALU_SLTIU_SELECTOR_B1),
    .ALU_SELECTOR_OP0(ALU_SLTIU_SELECTOR_OP0), .ALU_SELECTOR_OP1(ALU_SLTIU_SELECTOR_OP1),
    .WRITE_RF(WRITE_RF_SLTIU), .SELECTOR_ADDRESS0(SLTIU_SELECTOR_ADDRESS0));
  ADD add_1 (
    .CLK(CLK), .RST(RST), .POWER_IN(ADD), .POWER_OUT(END_ADD), .ALU_SELECTOR_A0(ALU_ADD_SELECTOR_A0),
    .ALU_SELECTOR_B0(ALU_ADD_SELECTOR_B0), .WRITE_RF(WRITE_RF_ADD));
  SUB sub_1 (
    .CLK(CLK), .RST(RST), .POWER_IN(SUB), .POWER_OUT(END_SUB), .ALU_SELECTOR_A0(ALU_SUB_SELECTOR_A0),
    .ALU_SELECTOR_OP0(ALU_SUB_SELECTOR_OP0), .ALU_SELECTOR_B0(ALU_SUB_SELECTOR_B0), .WRITE_RF(WRITE_RF_SUB));
  AND and_1 (
    .CLK(CLK), .RST(RST), .POWER_IN(AND), .POWER_OUT(END_AND), .ALU_SELECTOR_A0(ALU_AND_SELECTOR_A0),
    .ALU_SELECTOR_B0(ALU_AND_SELECTOR_B0), .ALU_SELECTOR_OP3(ALU_AND_SELECTOR_OP3), .WRITE_RF(WRITE_RF_AND));
  OR or_36 (
    .CLK(CLK), .RST(RST), .POWER_IN(OR), .POWER_OUT(END_OR), .ALU_SELECTOR_A0(ALU_OR_SELECTOR_A0),
    .ALU_SELECTOR_B0(ALU_OR_SELECTOR_B0), .ALU_SELECTOR_OP0(ALU_OR_SELECTOR_OP0),
    .ALU_SELECTOR_OP3(ALU_OR_SELECTOR_OP3), .WRITE_RF(WRITE_RF_OR));
  NOR nor_1 (
    .CLK(CLK), .RST(RST), .POWER_IN(NOR), .POWER_OUT(END_NOR), .ALU_SELECTOR_A0(ALU_NOR_SELECTOR_A0),
    .ALU_SELECTOR_B0(ALU_NOR_SELECTOR_B0), .ALU_SELECTOR_OP1(ALU_NOR_SELECTOR_OP1),
    .ALU_SELECTOR_OP3(ALU_NOR_SELECTOR_OP3), .WRITE_RF(WRITE_RF_NOR));
  XOR xor_1 (
    .CLK(CLK), .RST(RST), .POWER_IN(XOR), .POWER_OUT(END_XOR), .ALU_SELECTOR_A0(ALU_XOR_SELECTOR_A0),
    .ALU_SELECTOR_B0(ALU_XOR_SELECTOR_B0), .ALU_SELECTOR_OP0(ALU_XOR_SELECTOR_OP0),
    .ALU_SELECTOR_OP1(ALU_XOR_SELECTOR_OP1), .ALU_SELECTOR_OP3(ALU_XOR_SELECTOR_OP3), .WRITE_RF(WRITE_RF_XOR));
  SLT slt_1 (
    .CLK(CLK), .RST(RST), .POWER_IN(SLT), .POWER_OUT(STL_END), .ALU_SELECTOR_A0(ALU_SLT_SELECTOR_A0),
    .ALU_SELECTOR_B0(ALU_SLT_SELECTOR_B0), .ALU_SELECTOR_OP1(ALU_SLT_SELECTOR_OP1), .WRITE_RF(WRITE_RF_SLT));
  SLTU sltu_1 (
    .CLK(CLK), .RST(RST), .POWER_IN(SLTU), .POWER_OUT(SLTU_END), .ALU_SELECTOR_A0(ALU_SLTU_SELECTOR_A0),
    .ALU_SELECTOR_B0(ALU_SLTU_SELECTOR_B0), .ALU_SELECTOR_OP0(ALU_SLTU_SELECTOR_OP0),
    .ALU_SELECTOR_OP1(ALU_SLTU_SELECTOR_OP1), .WRITE_RF(WRITE_RF_SLTU));
  MULT mult_1 (
    .CLK(CLK), .RST(RST), .POWER_IN(MULT), .POWER_OUT(END_MULT), .ALU_SELECTOR_A0(ALU_MULT_SELECTOR_A0),
    .ALU_SELECTOR_B0(ALU_MULT_SELECTOR_B0), .ALU_SELECTOR_OP2(ALU_MULT_SELECTOR_OP2), .Load_HI(LOAD_HI_MULT),
    .Load_LO(LOAD_LO_MULT));
  MULTU multu_1 (
    .CLK(CLK), .RST(RST), .POWER_IN(MULTU), .POWER_OUT(END_MULTU), .ALU_SELECTOR_A0(ALU_MULTU_SELECTOR_A0),
    .ALU_SELECTOR_B0(ALU_MULTU_SELECTOR_B0), .ALU_SELECTOR_OP0(ALU_MULTU_SELECTOR_OP0),
    .Load_HI(LOAD_HI_MULTU), .Load_LO(LOAD_LO_MULTU), .ALU_SELECTOR_OP2(ALU_MULTU_SELECTOR_OP2));
  DIV div_1 (
    .CLK(CLK), .RST(RST), .POWER_IN(DIV), .POWER_OUT(END_DIV), .ALU_SELECTOR_A0(ALU_DIV_SELECTOR_A0),
    .ALU_SELECTOR_B0(ALU_DIV_SELECTOR_B0), .ALU_SELECTOR_OP1(ALU_DIV_SELECTOR_OP1),
    .ALU_SELECTOR_OP2(ALU_DIV_SELECTOR_OP2), .Load_HI(LOAD_HI_DIV), .Load_LO(LOAD_LO_DIV));
  DIVU divu_1 (
    .CLK(CLK), .RST(RST), .POWER_IN(DIVU), .POWER_OUT(END_DIVU), .ALU_SELECTOR_A0(ALU_DIVU_SELECTOR_A0),
    .ALU_SELECTOR_B0(ALU_DIVU_SELECTOR_B0), .ALU_SELECTOR_OP0(ALU_DIVU_SELECTOR_OP0),
    .ALU_SELECTOR_OP1(ALU_DIVU_SELECTOR_OP1), .ALU_SELECTOR_OP2(ALU_DIVU_SELECTOR_OP2),
    .Load_HI(LOAD_HI_DIVU), .Load_LO(LOAD_LO_DIVU));
  TTY tty_1 (.POWER_IN(TTY), .POWER_OUT(END_TTY), .TTY_ENABLE(TTY_ENABLE));
  NOP nop_1 (.POWER_IN(NOP), .POWER_OUT(END_NOP));
  HALT halt_1 (.POWER_IN(HALT), .POWER_OUT(END_HALT));
  FORWARD_PC forward_pc_1 (.POWER_IN(Forward_PC), .POWER_OUT(Single_Cycle), .Load_PC(LOAD_PC_0), .CLK(CLK), .RST(RST));

  assign ADDRESS_SELECTOR[1] = 1'b0;
  assign ALU_SELECTOR_A[1] = 1'b0;
  assign DATA_SELECTOR[1] = 1'b0;
  assign LoadInstructionRegister = Instruction_Avaiable;

  // Other names for the same wires on the sheet: SADDRESS0 = ADDRESS_SELECTOR[0]; ALU_OP0 = ALU_OP_SELECTOR[0];
  //   ALU_OP1 = ALU_OP_SELECTOR[1]; ALU_OP2 = ALU_OP_SELECTOR[2]; ALU_OP3 = ALU_OP_SELECTOR[3];
  //   J_SELECTOR_BRANCH0 = BRANCH_SELECTOR[0]; JR_SELECTOR_BRANCH1 = BRANCH_SELECTOR[1]; SDATA0 = DATA_SELECTOR[0];
  //   End_fetch_instruction = End_Fectch_Instruction; Instruction_ready = Instruction_Avaiable; NF = NEGATIVE_FLAG;
  //   Start_fetch_instruction = Start_Fectch_Instruction; TTY_ENBALE = TTY_ENABLE; ZF = ZERO_FLAG

  // Notes on the sheet:
  //   1
  //   TTY
  //   FetchInstruction
  //   KBD
  //   Control Signals
  //   Decode Instruction
  //   Program Counter
  //   Register File
  //   ALU Operation
  //   2
  //   Fetch Instruction
  //   Branch Control
  //   ALU
  //   Execution
  //   Flags
  //   PICK AN OPERATION
  //   3
  //   Algorithmic State Machines
  //   4
  //   HALT
endmodule

module FORWARD_PC (
  input  CLK,
  input  RST,
  input  POWER_IN,
  output Load_PC,
  output POWER_OUT
);

  D_Flip_Flop d_ff_1 (.clk(CLK), .D(POWER_IN), .Q(POWER_OUT), .reset(RST));  // open: Qn, preset, en

  assign Load_PC = POWER_IN;
endmodule

module ADD (
  input  CLK,
  input  RST,
  input  POWER_IN,
  output ALU_SELECTOR_A0,
  output ALU_SELECTOR_B0,
  output POWER_OUT,
  output WRITE_RF
);

  D_Flip_Flop d_ff_1 (.clk(CLK), .D(POWER_IN), .Q(POWER_OUT), .reset(RST));  // open: Qn, preset, en

  assign ALU_SELECTOR_A0 = POWER_IN;
  assign ALU_SELECTOR_B0 = POWER_IN;
  assign WRITE_RF = POWER_IN;
endmodule

module SUB (
  input  CLK,
  input  RST,
  input  POWER_IN,
  output ALU_SELECTOR_OP0,
  output ALU_SELECTOR_A0,
  output ALU_SELECTOR_B0,
  output POWER_OUT,
  output WRITE_RF
);

  D_Flip_Flop d_ff_1 (.clk(CLK), .D(POWER_IN), .Q(POWER_OUT), .reset(RST));  // open: Qn, preset, en

  assign ALU_SELECTOR_A0 = POWER_IN;
  assign ALU_SELECTOR_B0 = POWER_IN;
  assign ALU_SELECTOR_OP0 = POWER_IN;
  assign WRITE_RF = POWER_IN;
endmodule

module SLT (
  input  CLK,
  input  RST,
  input  POWER_IN,
  output ALU_SELECTOR_A0,
  output ALU_SELECTOR_B0,
  output ALU_SELECTOR_OP1,
  output POWER_OUT,
  output WRITE_RF
);

  D_Flip_Flop d_ff_1 (.clk(CLK), .D(POWER_IN), .Q(POWER_OUT), .reset(RST));  // open: Qn, preset, en

  assign ALU_SELECTOR_A0 = POWER_IN;
  assign ALU_SELECTOR_B0 = POWER_IN;
  assign ALU_SELECTOR_OP1 = POWER_IN;
  assign WRITE_RF = POWER_IN;
endmodule

module SLTU (
  input  CLK,
  input  RST,
  input  POWER_IN,
  output ALU_SELECTOR_A0,
  output ALU_SELECTOR_B0,
  output ALU_SELECTOR_OP0,
  output ALU_SELECTOR_OP1,
  output POWER_OUT,
  output WRITE_RF
);

  D_Flip_Flop d_ff_1 (.clk(CLK), .D(POWER_IN), .Q(POWER_OUT), .reset(RST));  // open: Qn, preset, en

  assign ALU_SELECTOR_A0 = POWER_IN;
  assign ALU_SELECTOR_B0 = POWER_IN;
  assign ALU_SELECTOR_OP0 = POWER_IN;
  assign ALU_SELECTOR_OP1 = POWER_IN;
  assign WRITE_RF = POWER_IN;
endmodule

module MULT (
  input  CLK,
  input  RST,
  input  POWER_IN,
  output ALU_SELECTOR_A0,
  output ALU_SELECTOR_B0,
  output ALU_SELECTOR_OP2,
  output POWER_OUT,
  output Load_HI,
  output Load_LO
);

  D_Flip_Flop d_ff_1 (.clk(CLK), .D(POWER_IN), .Q(POWER_OUT), .reset(RST));  // open: Qn, preset, en

  assign ALU_SELECTOR_A0 = POWER_IN;
  assign ALU_SELECTOR_B0 = POWER_IN;
  assign ALU_SELECTOR_OP2 = POWER_IN;
  assign Load_HI = POWER_IN;
  assign Load_LO = POWER_IN;
endmodule

module MULTU (
  input  CLK,
  input  RST,
  input  POWER_IN,
  output ALU_SELECTOR_A0,
  output ALU_SELECTOR_B0,
  output ALU_SELECTOR_OP0,
  output ALU_SELECTOR_OP2,
  output POWER_OUT,
  output Load_HI,
  output Load_LO
);

  D_Flip_Flop d_ff_1 (.clk(CLK), .D(POWER_IN), .Q(POWER_OUT), .reset(RST));  // open: Qn, preset, en

  assign ALU_SELECTOR_A0 = POWER_IN;
  assign ALU_SELECTOR_B0 = POWER_IN;
  assign ALU_SELECTOR_OP0 = POWER_IN;
  assign ALU_SELECTOR_OP2 = POWER_IN;
  assign Load_HI = POWER_IN;
  assign Load_LO = POWER_IN;
endmodule

module DIV (
  input  CLK,
  input  RST,
  input  POWER_IN,
  output ALU_SELECTOR_A0,
  output ALU_SELECTOR_B0,
  output ALU_SELECTOR_OP1,
  output ALU_SELECTOR_OP2,
  output POWER_OUT,
  output Load_HI,
  output Load_LO
);

  D_Flip_Flop d_ff_1 (.clk(CLK), .D(POWER_IN), .Q(POWER_OUT), .reset(RST));  // open: Qn, preset, en

  assign ALU_SELECTOR_A0 = POWER_IN;
  assign ALU_SELECTOR_B0 = POWER_IN;
  assign ALU_SELECTOR_OP1 = POWER_IN;
  assign ALU_SELECTOR_OP2 = POWER_IN;
  assign Load_HI = POWER_IN;
  assign Load_LO = POWER_IN;
endmodule

module DIVU (
  input  CLK,
  input  RST,
  input  POWER_IN,
  output ALU_SELECTOR_A0,
  output ALU_SELECTOR_B0,
  output ALU_SELECTOR_OP0,
  output ALU_SELECTOR_OP1,
  output ALU_SELECTOR_OP2,
  output POWER_OUT,
  output Load_HI,
  output Load_LO
);

  D_Flip_Flop d_ff_1 (.clk(CLK), .D(POWER_IN), .Q(POWER_OUT), .reset(RST));  // open: Qn, preset, en

  assign ALU_SELECTOR_A0 = POWER_IN;
  assign ALU_SELECTOR_B0 = POWER_IN;
  assign ALU_SELECTOR_OP0 = POWER_IN;
  assign ALU_SELECTOR_OP1 = POWER_IN;
  assign ALU_SELECTOR_OP2 = POWER_IN;
  assign Load_HI = POWER_IN;
  assign Load_LO = POWER_IN;
endmodule

module AND (
  input  CLK,
  input  RST,
  input  POWER_IN,
  output ALU_SELECTOR_A0,
  output ALU_SELECTOR_B0,
  output ALU_SELECTOR_OP3,
  output POWER_OUT,
  output WRITE_RF
);

  D_Flip_Flop d_ff_1 (.clk(CLK), .D(POWER_IN), .Q(POWER_OUT), .reset(RST));  // open: Qn, preset, en

  assign ALU_SELECTOR_A0 = POWER_IN;
  assign ALU_SELECTOR_B0 = POWER_IN;
  assign ALU_SELECTOR_OP3 = POWER_IN;
  assign WRITE_RF = POWER_IN;
endmodule

module OR (
  input  CLK,
  input  RST,
  input  POWER_IN,
  output ALU_SELECTOR_A0,
  output ALU_SELECTOR_B0,
  output ALU_SELECTOR_OP0,
  output ALU_SELECTOR_OP3,
  output POWER_OUT,
  output WRITE_RF
);

  D_Flip_Flop d_ff_1 (.clk(CLK), .D(POWER_IN), .Q(POWER_OUT), .reset(RST));  // open: Qn, preset, en

  assign ALU_SELECTOR_A0 = POWER_IN;
  assign ALU_SELECTOR_B0 = POWER_IN;
  assign ALU_SELECTOR_OP0 = POWER_IN;
  assign ALU_SELECTOR_OP3 = POWER_IN;
  assign WRITE_RF = POWER_IN;
endmodule

module NOR (
  input  CLK,
  input  RST,
  input  POWER_IN,
  output ALU_SELECTOR_A0,
  output ALU_SELECTOR_B0,
  output ALU_SELECTOR_OP1,
  output ALU_SELECTOR_OP3,
  output POWER_OUT,
  output WRITE_RF
);

  D_Flip_Flop d_ff_1 (.clk(CLK), .D(POWER_IN), .Q(POWER_OUT), .reset(RST));  // open: Qn, preset, en

  assign ALU_SELECTOR_A0 = POWER_IN;
  assign ALU_SELECTOR_B0 = POWER_IN;
  assign ALU_SELECTOR_OP1 = POWER_IN;
  assign ALU_SELECTOR_OP3 = POWER_IN;
  assign WRITE_RF = POWER_IN;
endmodule

module XOR (
  input  CLK,
  input  RST,
  input  POWER_IN,
  output ALU_SELECTOR_A0,
  output ALU_SELECTOR_B0,
  output ALU_SELECTOR_OP0,
  output ALU_SELECTOR_OP1,
  output ALU_SELECTOR_OP3,
  output POWER_OUT,
  output WRITE_RF
);

  D_Flip_Flop d_ff_1 (.clk(CLK), .D(POWER_IN), .Q(POWER_OUT), .reset(RST));  // open: Qn, preset, en

  assign ALU_SELECTOR_A0 = POWER_IN;
  assign ALU_SELECTOR_B0 = POWER_IN;
  assign ALU_SELECTOR_OP0 = POWER_IN;
  assign ALU_SELECTOR_OP1 = POWER_IN;
  assign ALU_SELECTOR_OP3 = POWER_IN;
  assign WRITE_RF = POWER_IN;
endmodule

module ADDI (
  input  CLK,
  input  RST,
  input  POWER_IN,
  output ALU_SELECTOR_A0,
  output ALU_SELECTOR_B0,
  output ALU_SELECTOR_B1,
  output POWER_OUT,
  output WRITE_RF,
  output SELECTOR_ADDRESS0
);

  D_Flip_Flop d_ff_1 (.clk(CLK), .D(POWER_IN), .Q(POWER_OUT), .reset(RST));  // open: Qn, preset, en

  assign ALU_SELECTOR_A0 = POWER_IN;
  assign ALU_SELECTOR_B0 = POWER_IN;
  assign ALU_SELECTOR_B1 = POWER_IN;
  assign SELECTOR_ADDRESS0 = POWER_IN;
  assign WRITE_RF = POWER_IN;
endmodule

module ANDI (
  input  CLK,
  input  RST,
  input  POWER_IN,
  output ALU_SELECTOR_A0,
  output ALU_SELECTOR_B0,
  output ALU_SELECTOR_B1,
  output ALU_SELECTOR_OP3,
  output POWER_OUT,
  output WRITE_RF,
  output SELECTOR_ADDRESS0
);

  D_Flip_Flop d_ff_1 (.clk(CLK), .D(POWER_IN), .Q(POWER_OUT), .reset(RST));  // open: Qn, preset, en

  assign ALU_SELECTOR_A0 = POWER_IN;
  assign ALU_SELECTOR_B0 = POWER_IN;
  assign ALU_SELECTOR_B1 = POWER_IN;
  assign ALU_SELECTOR_OP3 = POWER_IN;
  assign SELECTOR_ADDRESS0 = POWER_IN;
  assign WRITE_RF = POWER_IN;
endmodule

module ORI (
  input  CLK,
  input  RST,
  input  POWER_IN,
  output ALU_SELECTOR_A0,
  output ALU_SELECTOR_B0,
  output ALU_SELECTOR_B1,
  output ALU_SELECTOR_OP0,
  output ALU_SELECTOR_OP3,
  output POWER_OUT,
  output WRITE_RF,
  output SELECTOR_ADDRESS0
);

  D_Flip_Flop d_ff_1 (.clk(CLK), .D(POWER_IN), .Q(POWER_OUT), .reset(RST));  // open: Qn, preset, en

  assign ALU_SELECTOR_A0 = POWER_IN;
  assign ALU_SELECTOR_B0 = POWER_IN;
  assign ALU_SELECTOR_B1 = POWER_IN;
  assign ALU_SELECTOR_OP0 = POWER_IN;
  assign ALU_SELECTOR_OP3 = POWER_IN;
  assign SELECTOR_ADDRESS0 = POWER_IN;
  assign WRITE_RF = POWER_IN;
endmodule

module XORI (
  input  CLK,
  input  RST,
  input  POWER_IN,
  output ALU_SELECTOR_A0,
  output ALU_SELECTOR_B0,
  output ALU_SELECTOR_B1,
  output ALU_SELECTOR_OP0,
  output ALU_SELECTOR_OP1,
  output ALU_SELECTOR_OP3,
  output POWER_OUT,
  output WRITE_RF,
  output SELECTOR_ADDRESS0
);

  D_Flip_Flop d_ff_1 (.clk(CLK), .D(POWER_IN), .Q(POWER_OUT), .reset(RST));  // open: Qn, preset, en

  assign ALU_SELECTOR_A0 = POWER_IN;
  assign ALU_SELECTOR_B0 = POWER_IN;
  assign ALU_SELECTOR_B1 = POWER_IN;
  assign ALU_SELECTOR_OP0 = POWER_IN;
  assign ALU_SELECTOR_OP1 = POWER_IN;
  assign ALU_SELECTOR_OP3 = POWER_IN;
  assign SELECTOR_ADDRESS0 = POWER_IN;
  assign WRITE_RF = POWER_IN;
endmodule

module STLI (
  input  CLK,
  input  RST,
  input  POWER_IN,
  output ALU_SELECTOR_A0,
  output ALU_SELECTOR_B0,
  output ALU_SELECTOR_B1,
  output ALU_SELECTOR_OP1,
  output POWER_OUT,
  output WRITE_RF,
  output SELECTOR_ADDRESS0
);

  D_Flip_Flop d_ff_1 (.clk(CLK), .D(POWER_IN), .Q(POWER_OUT), .reset(RST));  // open: Qn, preset, en

  assign ALU_SELECTOR_A0 = POWER_IN;
  assign ALU_SELECTOR_B0 = POWER_IN;
  assign ALU_SELECTOR_B1 = POWER_IN;
  assign ALU_SELECTOR_OP1 = POWER_IN;
  assign SELECTOR_ADDRESS0 = POWER_IN;
  assign WRITE_RF = POWER_IN;
endmodule

module SLTIU (
  input  CLK,
  input  RST,
  input  POWER_IN,
  output ALU_SELECTOR_A0,
  output ALU_SELECTOR_B0,
  output ALU_SELECTOR_B1,
  output ALU_SELECTOR_OP0,
  output ALU_SELECTOR_OP1,
  output POWER_OUT,
  output WRITE_RF,
  output SELECTOR_ADDRESS0
);

  D_Flip_Flop d_ff_1 (.clk(CLK), .D(POWER_IN), .Q(POWER_OUT), .reset(RST));  // open: Qn, preset, en

  assign ALU_SELECTOR_A0 = POWER_IN;
  assign ALU_SELECTOR_B0 = POWER_IN;
  assign ALU_SELECTOR_B1 = POWER_IN;
  assign ALU_SELECTOR_OP0 = POWER_IN;
  assign ALU_SELECTOR_OP1 = POWER_IN;
  assign SELECTOR_ADDRESS0 = POWER_IN;
  assign WRITE_RF = POWER_IN;
endmodule

module NOP (
  input  POWER_IN,
  output POWER_OUT
);


  assign POWER_OUT = POWER_IN;
endmodule

module TTY (
  input  POWER_IN,
  output TTY_ENABLE,
  output POWER_OUT
);


  assign POWER_OUT = POWER_IN;
  assign TTY_ENABLE = POWER_IN;
endmodule

module HALT (
  input  POWER_IN,
  output POWER_OUT
);


  assign POWER_OUT = POWER_IN;
endmodule

module MFHI (
  input  CLK,
  input  RST,
  input  POWER_IN,
  output POWER_OUT,
  output WRITE_RF,
  output SELECTOR_DATA0
);

  D_Flip_Flop d_ff_1 (.clk(CLK), .D(POWER_IN), .Q(POWER_OUT), .reset(RST));  // open: Qn, preset, en

  assign SELECTOR_DATA0 = POWER_IN;
  assign WRITE_RF = POWER_IN;
endmodule

module MFLO (
  input  CLK,
  input  RST,
  input  POWER_IN,
  output POWER_OUT,
  output WRITE_RF,
  output SELECTOR_DATA1
);

  D_Flip_Flop d_ff_1 (.clk(CLK), .D(POWER_IN), .Q(POWER_OUT), .reset(RST));  // open: Qn, preset, en

  assign SELECTOR_DATA1 = POWER_IN;
  assign WRITE_RF = POWER_IN;
endmodule

module BEQ (
  input  CLK,
  input  ZERO_FLAG,
  input  RST,
  input  power_in,
  output SELECTOR_A0,
  output SELECTOR_B0,
  output Load_PC,
  output SELECTOR_OP0,
  output SELECTOR_B2,
  output power_out
);

  wire demultiplexer_1_out0, demultiplexer_1_out1, or_2_out;

  or or_1 (Load_PC, power_in, SELECTOR_B2);
  D_Flip_Flop d_ff_1 (.clk(CLK), .D(power_in), .Q(SELECTOR_A0), .reset(RST));  // open: Qn, preset, en
  Demultiplexer #(.enable("false")) demultiplexer_1 (
    .out0(demultiplexer_1_out0), .out1(demultiplexer_1_out1), .in(SELECTOR_A0), .sel(ZERO_FLAG));
  D_Flip_Flop d_ff_2 (.clk(CLK), .D(demultiplexer_1_out1), .Q(SELECTOR_B2), .reset(RST));  // open: Qn, preset, en
  or or_2 (or_2_out, demultiplexer_1_out0, SELECTOR_B2);
  D_Flip_Flop d_ff_3 (.clk(CLK), .D(or_2_out), .Q(power_out), .reset(RST));  // open: Qn, preset, en

  assign SELECTOR_B0 = SELECTOR_A0;
  assign SELECTOR_OP0 = SELECTOR_A0;

  // Other names for the same wires on the sheet: ALU_SELECTOR_A0 = SELECTOR_A0; ALU_SELECTOR_B0 = SELECTOR_A0;
  //   ALU_SELECTOR_OP0 = SELECTOR_A0; Load_PC0 = power_in; ALU_SELECTOR_B2 = SELECTOR_B2; Load_PC1 = SELECTOR_B2;
  //   ZF = ZERO_FLAG
endmodule

module BNE (
  input  CLK,
  input  ZERO_FLAG,
  input  RST,
  input  power_in,
  output SELECTOR_A0,
  output SELECTOR_B0,
  output Load_PC,
  output SELECTOR_OP0,
  output SELECTOR_B2,
  output power_out
);

  wire demultiplexer_1_out0, demultiplexer_1_out1, not_1_out, or_2_out;

  or or_1 (Load_PC, power_in, SELECTOR_B2);
  D_Flip_Flop d_ff_1 (.clk(CLK), .D(power_in), .Q(SELECTOR_A0), .reset(RST));  // open: Qn, preset, en
  Demultiplexer #(.enable("false")) demultiplexer_1 (
    .out0(demultiplexer_1_out0), .out1(demultiplexer_1_out1), .in(SELECTOR_A0), .sel(not_1_out));
  not not_1 (not_1_out, ZERO_FLAG);
  D_Flip_Flop d_ff_2 (.clk(CLK), .D(demultiplexer_1_out1), .Q(SELECTOR_B2), .reset(RST));  // open: Qn, preset, en
  or or_2 (or_2_out, demultiplexer_1_out0, SELECTOR_B2);
  D_Flip_Flop d_ff_3 (.clk(CLK), .D(or_2_out), .Q(power_out), .reset(RST));  // open: Qn, preset, en

  assign SELECTOR_B0 = SELECTOR_A0;
  assign SELECTOR_OP0 = SELECTOR_A0;

  // Other names for the same wires on the sheet: ALU_SELECTOR_A0 = SELECTOR_A0; ALU_SELECTOR_B0 = SELECTOR_A0;
  //   ALU_SELECTOR_OP0 = SELECTOR_A0; Load_PC0 = power_in; ALU_SELECTOR_B2 = SELECTOR_B2; Load_PC1 = SELECTOR_B2;
  //   ZF = ZERO_FLAG
endmodule

module BLEZ (
  input  CLK,
  input  ZERO_FLAG,
  input  RST,
  input  NEGATIVE_FLAG,
  input  power_in,
  output SELECTOR_A0,
  output SELECTOR_B0,
  output Load_PC,
  output SELECTOR_OP0,
  output SELECTOR_B1,
  output SELECTOR_B2,
  output power_out
);

  wire demultiplexer_1_out0, demultiplexer_1_out1, or_2_out, or_3_out;

  or or_1 (Load_PC, power_in, SELECTOR_B2);
  D_Flip_Flop d_ff_1 (.clk(CLK), .D(power_in), .Q(SELECTOR_A0), .reset(RST));  // open: Qn, preset, en
  Demultiplexer #(.enable("false")) demultiplexer_1 (
    .out0(demultiplexer_1_out0), .out1(demultiplexer_1_out1), .in(SELECTOR_A0), .sel(or_2_out));
  or or_2 (or_2_out, ZERO_FLAG, NEGATIVE_FLAG);
  D_Flip_Flop d_ff_2 (.clk(CLK), .D(demultiplexer_1_out1), .Q(SELECTOR_B2), .reset(RST));  // open: Qn, preset, en
  or or_3 (or_3_out, demultiplexer_1_out0, SELECTOR_B2);
  D_Flip_Flop d_ff_3 (.clk(CLK), .D(or_3_out), .Q(power_out), .reset(RST));  // open: Qn, preset, en

  assign SELECTOR_B0 = SELECTOR_A0;
  assign SELECTOR_B1 = SELECTOR_A0;
  assign SELECTOR_OP0 = SELECTOR_A0;

  // Other names for the same wires on the sheet: ALU_SELECTOR_A0 = SELECTOR_A0; ALU_SELECTOR_B0 = SELECTOR_A0;
  //   ALU_SELECTOR_B1 = SELECTOR_A0; ALU_SELECTOR_OP0 = SELECTOR_A0; Load_PC0 = power_in;
  //   ALU_SELECTOR_B2 = SELECTOR_B2; Load_PC1 = SELECTOR_B2; NF = NEGATIVE_FLAG; ZF = ZERO_FLAG
endmodule

module BGTZ (
  input  CLK,
  input  ZERO_FLAG,
  input  RST,
  input  NEGATIVE_FLAG,
  input  power_in,
  output SELECTOR_A0,
  output SELECTOR_B0,
  output Load_PC,
  output SELECTOR_OP0,
  output SELECTOR_B1,
  output SELECTOR_B2,
  output power_out
);

  wire demultiplexer_1_out0, demultiplexer_1_out1, not_1_out, or_2_out, or_3_out;

  or or_1 (Load_PC, power_in, SELECTOR_B2);
  D_Flip_Flop d_ff_1 (.clk(CLK), .D(power_in), .Q(SELECTOR_A0), .reset(RST));  // open: Qn, preset, en
  Demultiplexer #(.enable("false")) demultiplexer_1 (
    .out0(demultiplexer_1_out0), .out1(demultiplexer_1_out1), .in(SELECTOR_A0), .sel(not_1_out));
  not not_1 (not_1_out, or_2_out);
  or or_2 (or_2_out, ZERO_FLAG, NEGATIVE_FLAG);
  D_Flip_Flop d_ff_2 (.clk(CLK), .D(demultiplexer_1_out1), .Q(SELECTOR_B2), .reset(RST));  // open: Qn, preset, en
  or or_3 (or_3_out, demultiplexer_1_out0, SELECTOR_B2);
  D_Flip_Flop d_ff_3 (.clk(CLK), .D(or_3_out), .Q(power_out), .reset(RST));  // open: Qn, preset, en

  assign SELECTOR_B0 = SELECTOR_A0;
  assign SELECTOR_B1 = SELECTOR_A0;
  assign SELECTOR_OP0 = SELECTOR_A0;

  // Other names for the same wires on the sheet: ALU_SELECTOR_A0 = SELECTOR_A0; ALU_SELECTOR_B0 = SELECTOR_A0;
  //   ALU_SELECTOR_B1 = SELECTOR_A0; ALU_SELECTOR_OP0 = SELECTOR_A0; Load_PC0 = power_in;
  //   ALU_SELECTOR_B2 = SELECTOR_B2; Load_PC1 = SELECTOR_B2; NF = NEGATIVE_FLAG; ZF = ZERO_FLAG
endmodule

module BLTZ (
  input  CLK,
  input  RST,
  input  NEGATIVE_FLAG,
  input  power_in,
  output SELECTOR_A0,
  output SELECTOR_B0,
  output Load_PC,
  output SELECTOR_OP0,
  output SELECTOR_B1,
  output SELECTOR_B2,
  output power_out
);

  wire demultiplexer_1_out0, demultiplexer_1_out1, or_2_out;

  or or_1 (Load_PC, power_in, SELECTOR_B2);
  D_Flip_Flop d_ff_1 (.clk(CLK), .D(power_in), .Q(SELECTOR_A0), .reset(RST));  // open: Qn, preset, en
  Demultiplexer #(.enable("false")) demultiplexer_1 (
    .out0(demultiplexer_1_out0), .out1(demultiplexer_1_out1), .in(SELECTOR_A0), .sel(NEGATIVE_FLAG));
  D_Flip_Flop d_ff_2 (.clk(CLK), .D(demultiplexer_1_out1), .Q(SELECTOR_B2), .reset(RST));  // open: Qn, preset, en
  or or_2 (or_2_out, demultiplexer_1_out0, SELECTOR_B2);
  D_Flip_Flop d_ff_3 (.clk(CLK), .D(or_2_out), .Q(power_out), .reset(RST));  // open: Qn, preset, en

  assign SELECTOR_B0 = SELECTOR_A0;
  assign SELECTOR_B1 = SELECTOR_A0;
  assign SELECTOR_OP0 = SELECTOR_A0;

  // Other names for the same wires on the sheet: ALU_SELECTOR_A0 = SELECTOR_A0; ALU_SELECTOR_B0 = SELECTOR_A0;
  //   ALU_SELECTOR_B1 = SELECTOR_A0; ALU_SELECTOR_OP0 = SELECTOR_A0; Load_PC0 = power_in;
  //   ALU_SELECTOR_B2 = SELECTOR_B2; Load_PC1 = SELECTOR_B2; NF = NEGATIVE_FLAG
endmodule

module J (
  input  POWER_IN,
  output POWER_OUT,
  output SELECTOR_BRANCH0
);


  assign POWER_OUT = POWER_IN;
  assign SELECTOR_BRANCH0 = POWER_IN;
endmodule

module JR (
  input  POWER_IN,
  output POWER_OUT,
  output SELECTOR_BRANCH1
);


  assign POWER_OUT = POWER_IN;
  assign SELECTOR_BRANCH1 = POWER_IN;
endmodule
