// Logisim project C-DataPath.circ as structural Verilog: 1 circuit, main circuit DataPath
module DataPath (
  input  in_1,
  input  in_2,
  input  in_3,
  input  in_4,
  input  [31:0] in_5,
  output [31:0] out_6
);

  wire [31:0] IR;

  Register #(.width(32)) Program_Counter (.en(in_3), .Q(out_6), .clk(in_2), .clr(in_1));  // open: D
  Register #(.width(32)) Instruction_Register (.D(in_5), .en(in_4), .Q(IR), .clk(in_2), .clr(in_1));

  // Other names for the same wires on the sheet: CLK = in_2; FetchedInstruction[31:0] = in_5; LoadIR = in_4;
  //   LoadPC = in_3; RST = in_1
endmodule
